# Fritzing sketch Berna_Fly_Clock_Thermometer (saved by Fritzing 0.9.3b)

parts:
  ESP32-2432S028R = Adafruit HUZZAH32 ESP32 Feather [part_number="Adafruit #3405"]
  AM2301_(DHT21) = DHT22/AM2301 Humidity and Temperature Sensor
  GY-68_(BMP180) = Barometric Pressure Sensor - BMP180 Breakout (GY-68)
  DS3231 = ZS-042 RTC Module
  R2 = Temperature Sensor (Thermistor) [thermistor_type=NTC package=THT]
  R3 = Resistor [tolerance=±5% resistance=47k package=THT]

nets:
  N1: ESP32-2432S028R.A4_IO36, AM2301_(DHT21).DATA
  GND: ESP32-2432S028R.GND, AM2301_(DHT21).GND, DS3231.GND#0, R3.Pin_1
  3.3V: ESP32-2432S028R.3.3V, AM2301_(DHT21).VDD, DS3231.VCC#1, R2.pin_0
  N2: ESP32-2432S028R.IO27_A10, DS3231.SDA#2
  N3: ESP32-2432S028R.IO32_A7, R2.pin_1, R3.Pin_0
  N4: ESP32-2432S028R.SCL, DS3231.SCL#3
  N5: GY-68_(BMP180).VCC, DS3231.VCC#7
  N6: GY-68_(BMP180).GND, DS3231.GND#6
  N7: GY-68_(BMP180).SCL, DS3231.SCL#9
  N8: GY-68_(BMP180).SDA, DS3231.SDA#8
